# Fritzing sketch hookup (saved by Fritzing 0.9.1b)

parts:
  IMU1 = Adafruit 10-DOF IMU Breakout
  NEOPIXEL1 = Neopixel Strip -- Black (30/m) [part_number="8 Led Strip"]
  Arduino1 = Arduino Mini (Rev5)

nets:
  VIN: IMU1.VIN, NEOPIXEL1.+5V, Arduino1.5V
  GND: IMU1.GND, NEOPIXEL1.GND, Arduino1.GND
  N1: IMU1.SCL, Arduino1.A5
  N2: IMU1.SDA, Arduino1.A4
  N3: NEOPIXEL1.Din, Arduino1.D6_PWM

custom parts:
  Neopixel Strip -- Black (30/m): These NeoPixel strips have 30 digitally-addressable pixel LEDs per meter and are very affordable and are only 12.5 mm wide, 10 mm if you remove the strip from the casing.
